# Fritzing sketch Remote Power (saved by Fritzing 0.9.1b)
breadboards: 1

parts:
  Raspberry_Pi1 = Raspberry Pi B+
  U1 = Optocoupler [package=THT]
  R1 = Resistor [tolerance=±5% resistance=1k package="1206 [SMD]"]
  U2 = Optocoupler [package=THT]
  U3 = Optocoupler [package=THT]
  R2 = Resistor [tolerance=±5% resistance=1k package="1206 [SMD]"]
  R3 = Resistor [tolerance=±5% resistance=1k package="1206 [SMD]"]
  JP2 = Header 12 [package=1x12_machine-pin-header_lock.004]
  U4 = Optocoupler [package=THT]
  R4 = Resistor [tolerance=±5% resistance=1k package="1206 [SMD]"]

nets:
  N1: Raspberry_Pi1.GPIO13, R3.Pin_0
  N2: Raspberry_Pi1.GPIO19, R4.Pin_0
  N3: Raspberry_Pi1.GPIO21, R1.Pin_0
  N4: Raspberry_Pi1.GPIO20, R2.Pin_0
  N5: U1.Pin_1, R1.Pin_1
  N6: U1.Pin_2, U2.Pin_2, U3.Pin_2, U4.Pin_2
  N7: U1.Pin_4, JP2.3
  N8: U1.Pin_5, JP2.4
  N9: U2.Pin_1, R2.Pin_1
  N10: U2.Pin_4, JP2.1
  N11: U2.Pin_5, JP2.2
  N12: U3.Pin_1, R3.Pin_1
  N13: U3.Pin_4, JP2.6
  N14: U3.Pin_5, JP2.5
  N15: JP2.7, U4.Pin_5
  N16: JP2.8, U4.Pin_4
  N17: U4.Pin_1, R4.Pin_1
